// Digital circuit simulation.dig as structural Verilog
module simulation (
  input  NE555___ext_CLK__to_do,
  input  Int_NE555,
  output not_CLR,
  output CLK,
  output not_CLK,
  output CPC,
  output a0,
  output not_ERAM,
  output a2,
  output a7,
  output a4,
  output a5,
  output a6,
  output LMAR_L,
  output LMAR_H,
  output not_EMAR,
  output not_WRAM,
  output a4_2,
  output a5_2,
  output LRALU_IN,
  output LRALU_OUT,
  output ALUS0,
  output ALUS1,
  output ALUS2,
  output ALUS3,
  output ALUCN,
  output ALUM,
  output not_ERALU_OUT,
  output a7_2,
  output a0_2,
  output a1,
  output a2_2,
  output a3,
  output LC,
  output CHKZ,
  output CHKC,
  output not_CLC,
  output not_SEC,
  output LZ,
  output not_CSP,
  output SPD,
  output not_ESP,
  output a5_3,
  output a6_2,
  output a7_3,
  output a0_3,
  output a1_2,
  output a2_3,
  output a3_2,
  output LO,
  output CHKO,
  output not_EFR_out,
  output EFR_in,
  output not_CLR_2,
  output not_HLT,
  output CLK_2,
  output not_CLK_2,
  output CLR__not_used,
  output EEPROM_ready,
  output not_JMP,
  output LIR,
  output CHKI,
  output not_HLT_2,
  output not_ENA_I,
  output not_DIS_I,
  output not_NOP,
  output out_66,
  output EINT_OUT,
  output Reset_IRs,
  output Load_next_IR,
  output Inc_T,
  output Reset_T,
  output INT1,
  output INT2,
  output not_EA,
  output not_EX,
  output not_EY,
  output not_ETMP,
  output not_ED,
  output not_EE,
  output LA,
  output LX,
  output LY,
  output LTMP,
  output LD,
  output LE,
  output LOUT,
  output Enable_next_IR,
  output LPC_L,
  output LPC_H,
  output CPC_2,
  output EPC_L,
  output out_93,
  output out_94,
  output EPC_H,
  output EPC_ADDR,
  output clk_SP,
  output en_SPL,
  output not_U_D_SP,
  output en_SPH,
  output [15:0] Addr,
  output [7:0] Data,
  output [15:0] Ctrl
);

  wire _7400_1_pin5, _7400_1_pin8, _7400_1_pin10, _7400_1_pin11, _7400_1_pin12, _7400_2_pin6, _7400_2_pin10,
       _7400_3_pin3, _7400_3_pin6, _7400_3_pin8, _7400_3_pin11, _7400_4_pin11, _7400_5_pin3, _7400_5_pin8,
       _7404_1_pin9, _7404_2_pin12, _7408_1_pin1, _7408_1_pin2, _7408_1_pin6, _7408_2_pin6, _7408_2_pin9,
       _7408_2_pin10, _7408_2_pin11, _7408_3_pin3, _7408_3_pin6, _7410_1_pin6, _7410_1_pin10, _7410_1_pin11,
       _7432_1_pin9, _7432_1_pin10, _74138_1_pin1, _74138_1_pin2, _74138_1_pin3, _74161_1_pin15,
       _74161_2_pin15, _74161_3_pin15, _74373_1_pin8, _74373_1_pin13, _74373_1_pin14, _74373_1_pin17,
       _74373_2_pin8, _74373_2_pin13, _74373_2_pin14, _74373_2_pin17, ALU_H_pin2, ALU_H_pin7, ALU_H_pin9,
       ALU_H_pin10, ALU_H_pin11, ALU_L_pin2, ALU_L_pin9, ALU_L_pin10, ALU_L_pin11, and_1_out, and_2_out,
       and_3_out, CLOCK_BUF_pin2, CLOCK_BUF_pin8, CLOCK_BUF_pin11, CLOCK_BUF_pin13, Debouncer_2_pin2,
       Debouncer_2_pin3, Debouncer_2_pin8, Debouncer_2_pin10, Debouncer_2_pin11, Debouncer_2_pin12,
       Debouncer_pin8, Debouncer_pin10, ext_I_pin5, ext_I_pin9, FR_in_pin9, FR_in_pin11, FR_in_pin12,
       FR_in_pin14, FR_OUT_pin19, I_pin5, I_pin9, I_pin11, IC_L_pin15, Instructions_Control_Word_p17,
       Instructions_Control_Word_p19, Instructions_Control_Word_p20, Instructions_Control_Word_p21,
       nand_2_out, nand_5_out, Next_IR_pin2, Next_IR_pin5, Next_IR_pin6, Next_IR_pin9, Next_IR_pin12,
       Next_IR_pin15, Next_IR_pin16, Next_IR_pin19, not_1_out, not_2_out, not_3_out, not_4_out, not_5_out,
       not_6_out, PC_SP_Control_Word_p17, PC_SP_Control_Word_p19, PC_SP_Control_Word_p20,
       PC_SP_Control_Word_p21, RALU_IN_pin5, RALU_IN_pin6, RALU_IN_pin9, RALU_IN_pin15, RALU_IN_pin16,
       RALU_IN_pin19, RALU_OUT_pin8, RALU_OUT_pin18, RAM_p16, Registers_Control_Word_p18,
       Registers_Control_Word_p19, Registers_Control_Word_p20, ROM_p21, switchdt_1_p2, switchdt_1_p3,
       switchdt_2_p2, switchdt_2_p3, switchdt_3_p2, switchdt_3_p3;
  wire [3:0] _74161_1_pin14, _74161_2_pin14, _74161_3_pin14, _74161_4_pin14, _74245_2_pin5, _74245_2_pin9,
       OUT_pin2, OUT_pin12;

  // _28c64 Control_Word__6: pin names not known; wires that end beside it: 1'b0, a2_3, a1_2, a0_3, Ctrl[0], EFR_in, Ctrl[1], 1'b0, Ctrl[2], Ctrl[13], Ctrl[3], 1'b0, Ctrl[4], Ctrl[14], Ctrl[8], Ctrl[12], Ctrl[9], Ctrl[11], Ctrl[10], Ctrl[15], 1'b1, 1'b1
  // _28c64 Control_Word__5: pin names not known; wires that end beside it: 1'b0, not_CSP, LZ, not_SEC, Ctrl[0], a7_3, Ctrl[1], 1'b0, Ctrl[2], Ctrl[13], Ctrl[3], 1'b0, Ctrl[4], Ctrl[14], Ctrl[8], Ctrl[12], Ctrl[9], Ctrl[11], Ctrl[10], Ctrl[15], 1'b1, 1'b1
  _7408 _7408_1 (
    .pin1(_7408_1_pin1), .pin2(_7408_1_pin2), .pin3(not_JMP), .pin4(CLK), .pin5(LO), .pin6(_7408_1_pin6),
    .pin7(1'b0), .pin9(1'b1), .pin10(1'b1), .pin12(1'b1), .pin13(1'b1), .pin14(1'b1));  // open: pin8, pin11
  // _28c64 Control_Word__4: pin names not known; wires that end beside it: 1'b0, a2_2, a1, a0_2, Ctrl[0], not_CLC, Ctrl[1], 1'b0, Ctrl[2], Ctrl[13], Ctrl[3], 1'b0, Ctrl[4], Ctrl[14], Ctrl[8], Ctrl[12], Ctrl[9], Ctrl[11], Ctrl[10], Ctrl[15], 1'b1, 1'b1
  _74157 FR_in (
    .pin1(EFR_in), .pin2(1'b1), .pin3(1'b1), .pin5(1'b1), .pin6(1'b1), .pin8(1'b0), .pin9(FR_in_pin9),
    .pin10(Data[2]), .pin11(FR_in_pin11), .pin12(FR_in_pin12), .pin13(Data[3]), .pin14(FR_in_pin14),
    .pin15(1'b0), .pin16(1'b1));  // open: pin4, pin7
  _7400 _7400_1 (
    .pin1(1'b0), .pin2(1'b0), .pin4(CHKO), .pin5(_7400_1_pin5), .pin6(_7408_1_pin2), .pin7(1'b0),
    .pin8(_7400_1_pin8), .pin9(CHKC), .pin10(_7400_1_pin10), .pin11(_7400_1_pin11), .pin12(_7400_1_pin12),
    .pin13(CHKZ), .pin14(1'b1));  // open: pin3
  _7432 _7432_1 (
    .pin1(1'b0), .pin2(1'b0), .pin4(1'b0), .pin5(1'b0), .pin7(1'b0), .pin8(FR_in_pin14), .pin9(_7432_1_pin9),
    .pin10(_7432_1_pin10), .pin12(1'b1), .pin13(1'b1), .pin14(1'b1));  // open: pin3, pin6, pin11
  _7474 O (
    .pin1(1'b1), .pin2(1'b1), .pin3(1'b0), .pin4(1'b1), .pin7(1'b0), .pin8(_7400_1_pin5), .pin10(1'b1),
    .pin11(_7408_1_pin6), .pin12(FR_in_pin11), .pin13(1'b1), .pin14(1'b1));  // open: pin5, pin6, pin9
  _74245 FR_OUT (
    .pin1(1'b1), .pin2(1'b1), .pin3(1'b1), .pin4(_7400_1_pin10), .pin5(_7400_1_pin12), .pin6(1'b1),
    .pin7(1'b1), .pin8(1'b1), .pin9(1'b1), .pin10(1'b0), .pin11(Data[7]), .pin12(Data[6]), .pin13(Data[5]),
    .pin14(Data[4]), .pin15(Data[3]), .pin16(Data[2]), .pin17(Data[1]), .pin18(Data[0]),
    .pin19(FR_OUT_pin19), .pin20(1'b1));
  _7408 _7408_2 (
    .pin1(_7400_1_pin11), .pin2(_7400_1_pin8), .pin3(_7408_1_pin1), .pin4(CLK), .pin5(LZ),
    .pin6(_7408_2_pin6), .pin7(1'b0), .pin8(_7432_1_pin9), .pin9(_7408_2_pin9), .pin10(_7408_2_pin10),
    .pin11(_7408_2_pin11), .pin12(CLK), .pin13(LC), .pin14(1'b1));
  _7474 Z___C (
    .pin1(1'b1), .pin2(FR_in_pin12), .pin3(_7408_2_pin6), .pin4(1'b1), .pin5(_7400_1_pin12), .pin7(1'b0),
    .pin9(_7400_1_pin10), .pin10(not_SEC), .pin11(_7408_2_pin11), .pin12(FR_in_pin9), .pin13(not_CLC),
    .pin14(1'b1));  // open: pin6, pin8
  not not_1 (not_1_out, not_EFR_out);
  // _28c64 Control_Word__3: pin names not known; wires that end beside it: 1'b0, ALUS2, ALUS1, ALUS0, Ctrl[0], a7_2, Ctrl[1], 1'b0, Ctrl[2], Ctrl[13], Ctrl[3], 1'b0, Ctrl[4], Ctrl[14], Ctrl[8], Ctrl[12], Ctrl[9], Ctrl[11], Ctrl[10], Ctrl[15], 1'b1, 1'b1, 1'b0
  nand nand_1 (FR_OUT_pin19, not_1_out, EEPROM_ready);
  // _28c64 Control_Word__2: pin names not known; wires that end beside it: not_EMAR, LMAR_H, LMAR_L, Ctrl[0], LRALU_OUT, Ctrl[1], 1'b0, Ctrl[2], Ctrl[13], Ctrl[3], 1'b0, Ctrl[4], Ctrl[14], Ctrl[8], Ctrl[12], Ctrl[9], Ctrl[11], Ctrl[10], Ctrl[15], 1'b1, 1'b1, 1'b0, a2
  _74181 ALU_L (
    .pin1(Data[0]), .pin2(ALU_L_pin2), .pin3(ALUS3), .pin4(ALUS2), .pin5(ALUS1), .pin6(ALUS0), .pin7(ALUCN),
    .pin8(ALUM), .pin9(ALU_L_pin9), .pin10(ALU_L_pin10), .pin11(ALU_L_pin11), .pin12(1'b0));  // open: pin13, pin14, pin15, pin16, pin17, pin18, pin19, pin20, pin21, pin22, pin23, pin24
  _74181 ALU_H (
    .pin1(Data[4]), .pin2(ALU_H_pin2), .pin3(ALUS3), .pin4(ALUS2), .pin5(ALUS1), .pin6(ALUS0),
    .pin7(ALU_H_pin7), .pin8(ALUM), .pin9(ALU_H_pin9), .pin10(ALU_H_pin10), .pin11(ALU_H_pin11), .pin12(1'b0));  // open: pin13, pin14, pin15, pin16, pin17, pin18, pin19, pin20, pin21, pin22, pin23, pin24
  _7404 _7404_1 (
    .pin1(1'b0), .pin3(1'b0), .pin5(1'b0), .pin7(1'b0), .pin8(_7432_1_pin10), .pin9(_7404_1_pin9),
    .pin11(1'b1), .pin13(1'b1), .pin14(1'b1));  // open: pin2, pin4, pin6, pin10, pin12
  _74688 Z_BUS (
    .pin1(1'b0), .pin2(1'b0), .pin3(Data[0]), .pin4(1'b0), .pin5(Data[1]), .pin6(1'b0), .pin7(Data[2]),
    .pin8(1'b0), .pin9(Data[3]), .pin10(1'b0), .pin11(1'b0), .pin12(Data[4]), .pin13(1'b0), .pin14(Data[5]),
    .pin15(1'b0), .pin16(Data[6]), .pin17(1'b0), .pin18(Data[7]), .pin19(_7404_1_pin9), .pin20(1'b1));
  // _28c64 Control_Word__1: pin names not known; wires that end beside it: not_ERAM, a0, Ctrl[0], a7, Ctrl[1], 1'b0, Ctrl[2], Ctrl[13], Ctrl[3], 1'b0, Ctrl[4], Ctrl[14], Ctrl[8], Ctrl[12], Ctrl[9], Ctrl[11], Ctrl[10], Ctrl[15], 1'b1, 1'b1
  and and_1 (and_1_out, LMAR_L, Enable_next_IR);
  and and_2 (and_2_out, Enable_next_IR, LMAR_H);
  _74373 RALU_IN (
    .pin1(1'b0), .pin2(ALU_L_pin2), .pin3(Data[0]), .pin4(Data[1]), .pin5(RALU_IN_pin5), .pin6(RALU_IN_pin6),
    .pin7(Data[2]), .pin8(Data[3]), .pin9(RALU_IN_pin9), .pin10(1'b0), .pin11(LRALU_IN), .pin12(ALU_H_pin2),
    .pin13(Data[4]), .pin14(Data[5]), .pin15(RALU_IN_pin15), .pin16(RALU_IN_pin16), .pin17(Data[6]),
    .pin18(Data[7]), .pin19(RALU_IN_pin19), .pin20(1'b1));
  _74373 RALU_OUT (
    .pin1(not_ERALU_OUT), .pin2(Data[0]), .pin3(ALU_L_pin9), .pin4(ALU_L_pin10), .pin5(Data[1]),
    .pin6(Data[2]), .pin7(ALU_L_pin11), .pin8(RALU_OUT_pin8), .pin9(Data[3]), .pin10(1'b0),
    .pin11(LRALU_OUT), .pin12(Data[4]), .pin13(ALU_H_pin9), .pin14(ALU_H_pin10), .pin15(Data[5]),
    .pin16(Data[6]), .pin17(ALU_H_pin11), .pin18(RALU_OUT_pin18), .pin19(Data[7]), .pin20(1'b1));
  not not_2 (not_2_out, not_EMAR);
  nand nand_2 (nand_2_out, EEPROM_ready, not_2_out);
  _74373 MAR_L (
    .pin1(nand_2_out), .pin2(Addr[0]), .pin3(Data[0]), .pin4(Data[1]), .pin5(Addr[1]), .pin6(Addr[2]),
    .pin7(Data[2]), .pin8(Data[3]), .pin9(Addr[3]), .pin10(1'b0), .pin11(and_1_out), .pin12(Addr[4]),
    .pin13(Data[4]), .pin14(Data[5]), .pin15(Addr[5]), .pin16(Addr[6]), .pin17(Data[6]), .pin18(Data[7]),
    .pin19(Addr[7]), .pin20(1'b1));
  _74373 MAR_H (
    .pin1(nand_2_out), .pin2(Addr[8]), .pin3(Data[0]), .pin4(Data[1]), .pin5(Addr[9]), .pin6(Addr[10]),
    .pin7(Data[2]), .pin8(Data[3]), .pin9(Addr[11]), .pin10(1'b0), .pin11(and_2_out), .pin12(Addr[12]),
    .pin13(Data[4]), .pin14(Data[5]), .pin15(Addr[13]), .pin16(Addr[14]), .pin17(Data[6]), .pin18(Data[7]),
    .pin19(Addr[15]), .pin20(1'b1));
  _7404 _7404_2 (
    .pin1(1'b0), .pin3(1'b0), .pin5(1'b0), .pin7(1'b0), .pin9(1'b1), .pin11(1'b1), .pin12(_7404_2_pin12),
    .pin13(Addr[15]), .pin14(1'b1));  // open: pin2, pin4, pin6, pin8, pin10
  // _28c256 ROM: pin names not known; wires that end beside it: Addr[14], Addr[12], Addr[7], Addr[6], Addr[5], Addr[4], Addr[3], Addr[2], Addr[1], Addr[0], Data[0], Data[1], Data[2], 1'b0, 1'b1, 1'b1, Addr[13], Addr[8], Addr[9], Addr[11], ROM_p21, Addr[10], Addr[15], Data[7]
  // _62256 RAM: pin names not known; wires that end beside it: Addr[14], Addr[12], Addr[7], Addr[6], Addr[5], Addr[4], Addr[3], Addr[2], Addr[1], Addr[0], Data[0], Data[1], Data[2], 1'b0, 1'b1, RAM_p16, Addr[13], Addr[8], Addr[9], Addr[11], ROM_p21, Addr[10], _7404_2_pin12, Data[7]
  not not_3 (not_3_out, not_WRAM);
  not not_4 (not_4_out, not_ERAM);
  nand nand_3 (RAM_p16, CLK, not_3_out);
  not not_5 (not_5_out, not_ESP);
  nand nand_4 (ROM_p21, EEPROM_ready, not_4_out);
  nand nand_5 (nand_5_out, EEPROM_ready, not_5_out);
  not not_6 (not_6_out, not_CSP);
  and and_3 (and_3_out, EEPROM_ready, not_6_out);
  _74245 _74245_1 (
    .pin1(1'b1), .pin2(1'b1), .pin3(1'b1), .pin4(1'b1), .pin5(1'b1), .pin6(1'b1), .pin7(1'b1), .pin8(1'b1),
    .pin9(1'b1), .pin10(1'b0), .pin11(Addr[15]), .pin12(Addr[14]), .pin13(Addr[13]), .pin14(Addr[12]),
    .pin15(Addr[11]), .pin16(Addr[10]), .pin17(Addr[9]), .pin18(Addr[8]), .pin19(nand_5_out), .pin20(1'b1));
  not not_7 (en_SPL, and_3_out);
  Seven_Seg_Hex seven_seg_hex_1 (.d(_74245_2_pin9), .dp(1'b0));
  Seven_Seg_Hex seven_seg_hex_2 (.d(_74245_2_pin5), .dp(1'b0));
  _74245 _74245_2 (
    .pin1(1'b1), .pin2(_74245_2_pin5[0]), .pin3(_74245_2_pin5[1]), .pin4(_74245_2_pin5[2]),
    .pin5(_74245_2_pin5[3]), .pin6(_74245_2_pin9[0]), .pin7(_74245_2_pin9[1]), .pin8(_74245_2_pin9[2]),
    .pin9(_74245_2_pin9[3]), .pin10(1'b0), .pin11(Addr[7]), .pin12(Addr[6]), .pin13(Addr[5]),
    .pin14(Addr[4]), .pin15(Addr[3]), .pin16(Addr[2]), .pin17(Addr[1]), .pin18(Addr[0]), .pin19(nand_5_out),
    .pin20(1'b1));
  _74191 _74191_1 (
    .pin1(1'b1), .pin2(_74245_2_pin5[1]), .pin3(_74245_2_pin5[0]), .pin4(en_SPL), .pin5(not_U_D_SP),
    .pin6(_74245_2_pin5[2]), .pin7(_74245_2_pin5[3]), .pin8(1'b0), .pin9(1'b1), .pin10(1'b1),
    .pin11(not_CLR), .pin13(en_SPH), .pin14(CLK), .pin15(1'b1), .pin16(1'b1));  // open: pin12
  _74191 _74191_2 (
    .pin1(1'b1), .pin2(_74245_2_pin9[1]), .pin3(_74245_2_pin9[0]), .pin4(en_SPH), .pin5(not_U_D_SP),
    .pin6(_74245_2_pin9[2]), .pin7(_74245_2_pin9[3]), .pin8(1'b0), .pin9(1'b1), .pin10(1'b1),
    .pin11(not_CLR), .pin14(CLK), .pin15(1'b1), .pin16(1'b1));  // open: pin12, pin13
  Seven_Seg_Hex seven_seg_hex_3 (.d(Data[7:4]), .dp(1'b0));
  Seven_Seg_Hex seven_seg_hex_4 (.d(Data[3:0]), .dp(1'b0));
  Seven_Seg_Hex seven_seg_hex_5 (.d(Addr[15:12]), .dp(1'b0));
  Seven_Seg_Hex seven_seg_hex_6 (.d(Addr[11:8]), .dp(1'b0));
  Seven_Seg_Hex seven_seg_hex_7 (.d(Addr[7:4]), .dp(1'b0));
  Seven_Seg_Hex seven_seg_hex_8 (.d(Addr[3:0]), .dp(1'b0));
  Seven_Seg_Hex seven_seg_hex_9 (.d(Ctrl[15:12]), .dp(1'b0));
  Seven_Seg_Hex seven_seg_hex_10 (.d(Ctrl[11:8]), .dp(1'b0));
  Seven_Seg_Hex seven_seg_hex_11 (.d({3'b000, Ctrl[4]}), .dp(1'b0));
  Seven_Seg_Hex seven_seg_hex_12 (.d(Ctrl[3:0]), .dp(1'b0));
  // SwitchDT switchdt_1: pin names not known; wires that end beside it: 1'b0, switchdt_1_p2, switchdt_1_p3
  // SwitchDT switchdt_2: pin names not known; wires that end beside it: 1'b0, switchdt_2_p2, switchdt_2_p3
  // SwitchDT switchdt_3: pin names not known; wires that end beside it: 1'b0, switchdt_3_p2, switchdt_3_p3
  Seven_Seg_Hex seven_seg_hex_13 (.d(OUT_pin12), .dp(1'b0));
  Seven_Seg_Hex seven_seg_hex_14 (.d(OUT_pin2), .dp(1'b0));
  // SwitchDT switchdt_4: pin names not known; wires that end beside it: INT1, 1'b1
  // _28c64 PC_SP_Control_Word: pin names not known; wires that end beside it: 1'b1, 1'b1, Ctrl[15], Ctrl[10], Ctrl[11], Ctrl[9], Ctrl[12], Ctrl[8], Ctrl[14], Ctrl[4], 1'b0, Ctrl[3], Ctrl[13], Ctrl[2], 1'b0, Ctrl[1], PC_SP_Control_Word_p17, Ctrl[0], PC_SP_Control_Word_p19, PC_SP_Control_Word_p20, PC_SP_Control_Word_p21, 1'b0
  // _28c64 Instructions_Control_Word: pin names not known; wires that end beside it: 1'b1, 1'b1, Ctrl[15], Ctrl[10], Ctrl[11], Ctrl[9], Ctrl[12], Ctrl[8], Ctrl[14], Ctrl[4], 1'b0, Ctrl[3], Ctrl[13], Ctrl[2], 1'b0, Ctrl[1], Instructions_Control_Word_p17, Ctrl[0], Instructions_Control_Word_p19, Instructions_Control_Word_p20, Instructions_Control_Word_p21, 1'b0
  // SwitchDT switchdt_5: pin names not known; wires that end beside it: INT2, 1'b1
  PullUp pullup_1 (.out(switchdt_1_p3));
  PullUp pullup_2 (.out(switchdt_2_p3));
  PullUp pullup_3 (.out(switchdt_3_p3));
  // _28c64 Registers_Control_Word: pin names not known; wires that end beside it: 1'b1, 1'b1, Ctrl[15], Ctrl[10], Ctrl[11], Ctrl[9], Ctrl[12], Ctrl[8], Ctrl[14], Ctrl[4], 1'b0, Ctrl[3], Ctrl[13], Ctrl[2], 1'b0, Ctrl[1], Ctrl[0], Registers_Control_Word_p18, Registers_Control_Word_p19, Registers_Control_Word_p20, 1'b0
  PullUp pullup_4 (.out(switchdt_1_p2));
  PullUp pullup_5 (.out(switchdt_2_p2));
  PullUp pullup_6 (.out(switchdt_3_p2));
  _7400 Debouncer (
    .pin1(switchdt_1_p2), .pin2(CLR__not_used), .pin3(not_CLR), .pin4(not_CLR), .pin5(switchdt_1_p3),
    .pin6(CLR__not_used), .pin7(1'b0), .pin8(Debouncer_pin8), .pin9(switchdt_2_p3), .pin10(Debouncer_pin10),
    .pin11(Debouncer_pin10), .pin12(Debouncer_pin8), .pin13(switchdt_2_p2), .pin14(1'b1));
  _7400 Debouncer_2 (
    .pin1(switchdt_3_p2), .pin2(Debouncer_2_pin2), .pin3(Debouncer_2_pin3), .pin4(Debouncer_2_pin3),
    .pin5(switchdt_3_p3), .pin6(Debouncer_2_pin2), .pin7(1'b0), .pin8(Debouncer_2_pin8),
    .pin9(Debouncer_2_pin2), .pin10(Debouncer_2_pin10), .pin11(Debouncer_2_pin11), .pin12(Debouncer_2_pin12),
    .pin13(Debouncer_2_pin8), .pin14(1'b1));
  _7404 CLOCK_BUF (
    .pin1(Debouncer_2_pin11), .pin2(CLOCK_BUF_pin2), .pin3(CLOCK_BUF_pin2), .pin4(CLK),
    .pin5(Debouncer_2_pin11), .pin6(Enable_next_IR), .pin7(1'b0), .pin8(CLOCK_BUF_pin8),
    .pin9(NE555___ext_CLK__to_do), .pin10(EEPROM_ready), .pin11(CLOCK_BUF_pin11), .pin12(CLOCK_BUF_pin11),
    .pin13(CLOCK_BUF_pin13), .pin14(1'b1));
  Seven_Seg_Hex seven_seg_hex_15 (.d(_74161_4_pin14), .dp(1'b0));
  Seven_Seg_Hex seven_seg_hex_16 (.d(_74161_3_pin14), .dp(1'b0));
  _7400 _7400_2 (
    .pin1(Debouncer_pin10), .pin2(Debouncer_2_pin3), .pin3(Debouncer_2_pin12), .pin4(Debouncer_2_pin11),
    .pin5(Debouncer_2_pin11), .pin6(_7400_2_pin6), .pin7(1'b0), .pin9(_7400_2_pin6), .pin10(_7400_2_pin10),
    .pin11(_7400_2_pin10), .pin12(NE555___ext_CLK__to_do), .pin13(NE555___ext_CLK__to_do), .pin14(1'b1));  // open: pin8
  _74107 _74107_1 (
    .pin1(not_HLT), .pin3(Debouncer_2_pin10), .pin4(not_HLT), .pin7(1'b0), .pin8(1'b0), .pin9(1'b0),
    .pin10(1'b0), .pin11(1'b0), .pin12(NE555___ext_CLK__to_do), .pin13(not_CLR), .pin14(1'b1));  // open: pin2, pin5, pin6
  Seven_Seg_Hex seven_seg_hex_17 (.d(_74161_2_pin14), .dp(1'b0));
  Seven_Seg_Hex seven_seg_hex_18 (.d(_74161_1_pin14), .dp(1'b0));
  _7474 _7474_1 (
    .pin1(1'b1), .pin2(1'b0), .pin3(Enable_next_IR), .pin4(CLOCK_BUF_pin8), .pin5(CLOCK_BUF_pin13),
    .pin7(1'b0), .pin10(1'b1), .pin11(1'b1), .pin12(1'b1), .pin13(1'b1), .pin14(1'b1));  // open: pin6, pin8, pin9
  _74373 _74373_1 (
    .pin1(1'b0), .pin2(LPC_L), .pin3(PC_SP_Control_Word_p19), .pin4(PC_SP_Control_Word_p20), .pin5(LPC_H),
    .pin6(CPC_2), .pin7(PC_SP_Control_Word_p21), .pin8(_74373_1_pin8), .pin9(EPC_L), .pin10(1'b0),
    .pin11(EEPROM_ready), .pin12(EPC_H), .pin13(_74373_1_pin13), .pin14(_74373_1_pin14), .pin15(EPC_ADDR),
    .pin16(out_93), .pin17(_74373_1_pin17), .pin18(PC_SP_Control_Word_p17), .pin19(out_94), .pin20(1'b1));
  _74138 _74138_1 (
    .pin1(_74138_1_pin1), .pin2(_74138_1_pin2), .pin3(_74138_1_pin3), .pin4(1'b0), .pin5(1'b0),
    .pin6(EEPROM_ready), .pin8(1'b0), .pin9(not_EE), .pin10(not_ED), .pin11(not_ETMP), .pin12(not_EY),
    .pin13(not_EX), .pin14(not_EA), .pin16(1'b1));  // open: pin7, pin15
  _74238 _74238_1 (
    .pin1(Registers_Control_Word_p18), .pin2(Registers_Control_Word_p19), .pin3(Registers_Control_Word_p20),
    .pin4(1'b0), .pin5(1'b0), .pin6(CLK), .pin7(LOUT), .pin8(1'b0), .pin9(LE), .pin10(LD), .pin11(LTMP),
    .pin12(LY), .pin13(LX), .pin14(LA), .pin16(1'b1));  // open: pin15
  _74373 _74373_2 (
    .pin1(1'b0), .pin2(LIR), .pin3(Instructions_Control_Word_p19), .pin4(Instructions_Control_Word_p20),
    .pin5(CHKI), .pin6(not_HLT), .pin7(Instructions_Control_Word_p21), .pin8(_74373_2_pin8),
    .pin9(not_ENA_I), .pin10(1'b0), .pin11(EEPROM_ready), .pin12(out_66), .pin13(_74373_2_pin13),
    .pin14(_74373_2_pin14), .pin15(EINT_OUT), .pin16(not_DIS_I), .pin17(_74373_2_pin17),
    .pin18(Instructions_Control_Word_p17), .pin19(not_NOP), .pin20(1'b1));
  _7400 _7400_3 (
    .pin1(LPC_L), .pin2(CLK), .pin3(_7400_3_pin3), .pin4(LPC_H), .pin5(CLK), .pin6(_7400_3_pin6),
    .pin7(1'b0), .pin8(_7400_3_pin8), .pin9(EEPROM_ready), .pin10(EPC_H), .pin11(_7400_3_pin11),
    .pin12(EEPROM_ready), .pin13(EPC_L), .pin14(1'b1));
  _7400 _7400_4 (
    .pin1(1'b0), .pin2(1'b0), .pin4(1'b0), .pin5(1'b0), .pin7(1'b0), .pin9(1'b1), .pin10(1'b1),
    .pin11(_7400_4_pin11), .pin12(EEPROM_ready), .pin13(EPC_ADDR), .pin14(1'b1));  // open: pin3, pin6, pin8
  _74373 A (
    .pin1(not_EA), .pin2(Data[0]), .pin3(Data[0]), .pin4(Data[1]), .pin5(Data[1]), .pin6(Data[2]),
    .pin7(Data[2]), .pin8(Data[3]), .pin9(Data[3]), .pin10(1'b0), .pin11(LA), .pin12(Data[4]),
    .pin13(Data[4]), .pin14(Data[5]), .pin15(Data[5]), .pin16(Data[6]), .pin17(Data[6]), .pin18(Data[7]),
    .pin19(Data[7]), .pin20(1'b1));
  _7408 _7408_3 (
    .pin1(not_CLR), .pin2(not_DIS_I), .pin3(_7408_3_pin3), .pin4(LIR), .pin5(not_CLR), .pin6(_7408_3_pin6),
    .pin7(1'b0), .pin8(Load_next_IR), .pin9(CLK), .pin10(_7408_3_pin6), .pin11(Reset_T), .pin12(not_NOP),
    .pin13(not_CLR), .pin14(1'b1));
  _7474 I (
    .pin1(_7408_3_pin3), .pin2(1'b1), .pin3(1'b0), .pin4(not_ENA_I), .pin5(I_pin5), .pin7(1'b0),
    .pin9(I_pin9), .pin10(1'b1), .pin11(I_pin11), .pin12(1'b1), .pin13(not_ENA_I), .pin14(1'b1));  // open: pin6, pin8
  _74373 X (
    .pin1(not_EX), .pin2(Data[0]), .pin3(Data[0]), .pin4(Data[1]), .pin5(Data[1]), .pin6(Data[2]),
    .pin7(Data[2]), .pin8(Data[3]), .pin9(Data[3]), .pin10(1'b0), .pin11(LX), .pin12(Data[4]),
    .pin13(Data[4]), .pin14(Data[5]), .pin15(Data[5]), .pin16(Data[6]), .pin17(Data[6]), .pin18(Data[7]),
    .pin19(Data[7]), .pin20(1'b1));
  _7410 _7410_1 (
    .pin1(1'b0), .pin2(1'b0), .pin3(I_pin5), .pin4(I_pin9), .pin5(CHKI), .pin6(_7410_1_pin6), .pin7(1'b0),
    .pin8(I_pin11), .pin9(Int_NE555), .pin10(_7410_1_pin10), .pin11(_7410_1_pin11), .pin13(1'b1), .pin14(1'b1));  // open: pin12
  PullDown pulldown_1 (.out(INT1));
  PullDown pulldown_2 (.out(INT2));
  _7400 _7400_5 (
    .pin1(_7410_1_pin6), .pin2(_7410_1_pin6), .pin3(_7400_5_pin3), .pin4(1'b0), .pin5(1'b0), .pin7(1'b0),
    .pin8(_7400_5_pin8), .pin9(EEPROM_ready), .pin10(EINT_OUT), .pin11(Reset_IRs), .pin12(CLK),
    .pin13(_7400_5_pin3), .pin14(1'b1));  // open: pin6
  _7474 ext_I (
    .pin1(not_ENA_I), .pin2(1'b1), .pin3(INT1), .pin4(1'b1), .pin5(ext_I_pin5), .pin6(_7410_1_pin11),
    .pin7(1'b0), .pin8(_7410_1_pin10), .pin9(ext_I_pin9), .pin10(1'b1), .pin11(INT2), .pin12(1'b1),
    .pin13(not_ENA_I), .pin14(1'b1));
  _74373 Y (
    .pin1(not_EY), .pin2(Data[0]), .pin3(Data[0]), .pin4(Data[1]), .pin5(Data[1]), .pin6(Data[2]),
    .pin7(Data[2]), .pin8(Data[3]), .pin9(Data[3]), .pin10(1'b0), .pin11(LY), .pin12(Data[4]),
    .pin13(Data[4]), .pin14(Data[5]), .pin15(Data[5]), .pin16(Data[6]), .pin17(Data[6]), .pin18(Data[7]),
    .pin19(Data[7]), .pin20(1'b1));
  _74161 _74161_1 (
    .pin1(not_CLR), .pin2(Enable_next_IR), .pin3(Data[0]), .pin4(Data[1]), .pin5(Data[2]), .pin6(Data[3]),
    .pin7(CPC_2), .pin8(1'b0), .pin9(_7400_3_pin3), .pin10(1'b1), .pin11(_74161_1_pin14[3]),
    .pin12(_74161_1_pin14[2]), .pin13(_74161_1_pin14[1]), .pin14(_74161_1_pin14[0]), .pin15(_74161_1_pin15),
    .pin16(1'b1));
  _74161 _74161_2 (
    .pin1(not_CLR), .pin2(Enable_next_IR), .pin3(Data[4]), .pin4(Data[5]), .pin5(Data[6]), .pin6(Data[7]),
    .pin7(CPC_2), .pin8(1'b0), .pin9(_7400_3_pin3), .pin10(_74161_1_pin15), .pin11(_74161_2_pin14[3]),
    .pin12(_74161_2_pin14[2]), .pin13(_74161_2_pin14[1]), .pin14(_74161_2_pin14[0]), .pin15(_74161_2_pin15),
    .pin16(1'b1));
  _74161 _74161_3 (
    .pin1(not_CLR), .pin2(Enable_next_IR), .pin3(Data[0]), .pin4(Data[1]), .pin5(Data[2]), .pin6(Data[3]),
    .pin7(CPC_2), .pin8(1'b0), .pin9(_7400_3_pin6), .pin10(_74161_2_pin15), .pin11(_74161_3_pin14[3]),
    .pin12(_74161_3_pin14[2]), .pin13(_74161_3_pin14[1]), .pin14(_74161_3_pin14[0]), .pin15(_74161_3_pin15),
    .pin16(1'b1));
  _74161 _74161_4 (
    .pin1(not_CLR), .pin2(Enable_next_IR), .pin3(Data[4]), .pin4(Data[5]), .pin5(Data[6]), .pin6(Data[7]),
    .pin7(CPC_2), .pin8(1'b0), .pin9(_7400_3_pin6), .pin10(_74161_3_pin15), .pin11(_74161_4_pin14[3]),
    .pin12(_74161_4_pin14[2]), .pin13(_74161_4_pin14[1]), .pin14(_74161_4_pin14[0]), .pin16(1'b1));  // open: pin15
  _74245 INT_OUT (
    .pin1(1'b1), .pin2(ext_I_pin5), .pin3(ext_I_pin9), .pin4(1'b1), .pin5(1'b1), .pin6(1'b1), .pin7(1'b1),
    .pin8(1'b1), .pin9(1'b1), .pin10(1'b0), .pin11(Data[7]), .pin12(Data[6]), .pin13(Data[5]),
    .pin14(Data[4]), .pin15(Data[3]), .pin16(Data[2]), .pin17(Data[1]), .pin18(Data[0]),
    .pin19(_7400_5_pin8), .pin20(1'b1));
  _74163 IC_L (
    .pin1(Reset_T), .pin2(Enable_next_IR), .pin3(1'b0), .pin4(1'b0), .pin5(1'b0), .pin6(1'b0), .pin7(1'b1),
    .pin8(1'b0), .pin9(not_JMP), .pin10(1'b1), .pin11(Ctrl[3]), .pin12(Ctrl[2]), .pin13(Ctrl[1]),
    .pin14(Ctrl[0]), .pin15(IC_L_pin15), .pin16(1'b1));
  _74163 IC_H (
    .pin1(Reset_T), .pin2(Enable_next_IR), .pin3(1'b1), .pin4(1'b0), .pin5(1'b0), .pin6(1'b0), .pin7(1'b1),
    .pin8(1'b0), .pin9(not_JMP), .pin10(IC_L_pin15), .pin14(Ctrl[4]), .pin16(1'b1));  // open: pin11, pin12, pin13, pin15
  _74373 TMP (
    .pin1(not_ETMP), .pin2(Data[0]), .pin3(Data[0]), .pin4(Data[1]), .pin5(Data[1]), .pin6(Data[2]),
    .pin7(Data[2]), .pin8(Data[3]), .pin9(Data[3]), .pin10(1'b0), .pin11(LTMP), .pin12(Data[4]),
    .pin13(Data[4]), .pin14(Data[5]), .pin15(Data[5]), .pin16(Data[6]), .pin17(Data[6]), .pin18(Data[7]),
    .pin19(Data[7]), .pin20(1'b1));
  _74245 _74245_3 (
    .pin1(1'b1), .pin2(_74161_1_pin14[0]), .pin3(_74161_1_pin14[1]), .pin4(_74161_1_pin14[2]),
    .pin5(_74161_1_pin14[3]), .pin6(_74161_2_pin14[0]), .pin7(_74161_2_pin14[1]), .pin8(_74161_2_pin14[2]),
    .pin9(_74161_2_pin14[3]), .pin10(1'b0), .pin11(Data[7]), .pin12(Data[6]), .pin13(Data[5]),
    .pin14(Data[4]), .pin15(Data[3]), .pin16(Data[2]), .pin17(Data[1]), .pin18(Data[0]),
    .pin19(_7400_3_pin11), .pin20(1'b1));
  _74245 _74245_4 (
    .pin1(1'b1), .pin2(_74161_3_pin14[0]), .pin3(_74161_3_pin14[1]), .pin4(_74161_3_pin14[2]),
    .pin5(_74161_3_pin14[3]), .pin6(_74161_4_pin14[0]), .pin7(_74161_4_pin14[1]), .pin8(_74161_4_pin14[2]),
    .pin9(_74161_4_pin14[3]), .pin10(1'b0), .pin11(Data[7]), .pin12(Data[6]), .pin13(Data[5]),
    .pin14(Data[4]), .pin15(Data[3]), .pin16(Data[2]), .pin17(Data[1]), .pin18(Data[0]),
    .pin19(_7400_3_pin8), .pin20(1'b1));
  _74373 D (
    .pin1(not_ED), .pin2(Data[0]), .pin3(Data[0]), .pin4(Data[1]), .pin5(Data[1]), .pin6(Data[2]),
    .pin7(Data[2]), .pin8(Data[3]), .pin9(Data[3]), .pin10(1'b0), .pin11(LD), .pin12(Data[4]),
    .pin13(Data[4]), .pin14(Data[5]), .pin15(Data[5]), .pin16(Data[6]), .pin17(Data[6]), .pin18(Data[7]),
    .pin19(Data[7]), .pin20(1'b1));
  _74273 Next_IR (
    .pin1(Reset_IRs), .pin2(Next_IR_pin2), .pin3(Data[0]), .pin4(Data[1]), .pin5(Next_IR_pin5),
    .pin6(Next_IR_pin6), .pin7(Data[2]), .pin8(Data[3]), .pin9(Next_IR_pin9), .pin10(1'b0),
    .pin11(Load_next_IR), .pin12(Next_IR_pin12), .pin13(Data[4]), .pin14(Data[5]), .pin15(Next_IR_pin15),
    .pin16(Next_IR_pin16), .pin17(Data[6]), .pin18(Data[7]), .pin19(Next_IR_pin19), .pin20(1'b1));
  _74245 _74245_5 (
    .pin1(1'b1), .pin2(_74161_1_pin14[0]), .pin3(_74161_1_pin14[1]), .pin4(_74161_1_pin14[2]),
    .pin5(_74161_1_pin14[3]), .pin6(_74161_2_pin14[0]), .pin7(_74161_2_pin14[1]), .pin8(_74161_2_pin14[2]),
    .pin9(_74161_2_pin14[3]), .pin10(1'b0), .pin11(Addr[7]), .pin12(Addr[6]), .pin13(Addr[5]),
    .pin14(Addr[4]), .pin15(Addr[3]), .pin16(Addr[2]), .pin17(Addr[1]), .pin18(Addr[0]),
    .pin19(_7400_4_pin11), .pin20(1'b1));
  _74245 _74245_6 (
    .pin1(1'b1), .pin2(_74161_3_pin14[0]), .pin3(_74161_3_pin14[1]), .pin4(_74161_3_pin14[2]),
    .pin5(_74161_3_pin14[3]), .pin6(_74161_4_pin14[0]), .pin7(_74161_4_pin14[1]), .pin8(_74161_4_pin14[2]),
    .pin9(_74161_4_pin14[3]), .pin10(1'b0), .pin11(Addr[15]), .pin12(Addr[14]), .pin13(Addr[13]),
    .pin14(Addr[12]), .pin15(Addr[11]), .pin16(Addr[10]), .pin17(Addr[9]), .pin18(Addr[8]),
    .pin19(_7400_4_pin11), .pin20(1'b1));
  _74373 E (
    .pin1(not_EE), .pin2(Data[0]), .pin3(Data[0]), .pin4(Data[1]), .pin5(Data[1]), .pin6(Data[2]),
    .pin7(Data[2]), .pin8(Data[3]), .pin9(Data[3]), .pin10(1'b0), .pin11(LE), .pin12(Data[4]),
    .pin13(Data[4]), .pin14(Data[5]), .pin15(Data[5]), .pin16(Data[6]), .pin17(Data[6]), .pin18(Data[7]),
    .pin19(Data[7]), .pin20(1'b1));
  _74273 IR (
    .pin1(1'b1), .pin2(Ctrl[8]), .pin3(Next_IR_pin2), .pin4(Next_IR_pin5), .pin5(Ctrl[9]), .pin6(Ctrl[10]),
    .pin7(Next_IR_pin6), .pin8(Next_IR_pin9), .pin9(Ctrl[11]), .pin10(1'b0), .pin11(Enable_next_IR),
    .pin12(Ctrl[12]), .pin13(Next_IR_pin12), .pin14(Next_IR_pin15), .pin15(Ctrl[13]), .pin16(Ctrl[14]),
    .pin17(Next_IR_pin16), .pin18(Next_IR_pin19), .pin19(Ctrl[15]), .pin20(1'b1));
  _74373 OUT (
    .pin1(1'b0), .pin2(OUT_pin2[0]), .pin3(Data[0]), .pin4(Data[1]), .pin5(OUT_pin2[1]), .pin6(OUT_pin2[2]),
    .pin7(Data[2]), .pin8(Data[3]), .pin9(OUT_pin2[3]), .pin10(1'b0), .pin11(LOUT), .pin12(OUT_pin12[0]),
    .pin13(Data[4]), .pin14(Data[5]), .pin15(OUT_pin12[1]), .pin16(OUT_pin12[2]), .pin17(Data[6]),
    .pin18(Data[7]), .pin19(OUT_pin12[3]), .pin20(1'b1));

  assign CLK_2 = CLK;
  assign clk_SP = CLK;
  assign Ctrl[7:5] = 3'b000;
  assign Inc_T = Enable_next_IR;
  assign not_CLK = Enable_next_IR;
  assign not_CLK_2 = Enable_next_IR;
  assign not_CLR_2 = not_CLR;
  assign not_HLT_2 = not_HLT;
  assign SPD = not_U_D_SP;

  // Notes on the sheet:
  //   NE555___ext_CLK__to_do: Hz: 1000
  //   Int_NE555: Hz: 10
  //   Data Bus
  //   Address Bus
  //   Control Bus (IC + t)
  //   Control Bus
  //   Clock & Ctrl board
  //   Registers board
  //   Instructions board
  //   CLEAR (push)
  //   STEP (push)
  //   MANUAL/AUTO (switch)
  //   Out Reg
  //   ext INT 1
  //   not CLR
  //   not HLT
  //   CLK
  //   not CLK
  //   EEPROM ready
  //   ext INT 2
  //   CLK/2
  //   EEPROM ready is activated 1/4 of cycle after CLK falling.
  //   Use this signal to react and avoid eeprom glitch
  //   PC
  //   Registry output is activated on EEPROM ready signal
  //   Registry load is activated later, on CLK rising up
  //   Enable interrupt 
  //   on CLI
  //   Disable interrupt
  //   on SEI or CLR
  //   CHKI & INT Enabled 
  //   & INT value
  //   (nand)
  //   Timer INT
  //   To avoid conflicts on power up, the OE is inverted.
  //   (on power up exit of buffer is 0)
  //   Output is enabled on eeprom ready only
  //   IC reset (SR) is activated on NOP or CLR (go to T=0)
  //   IC preset (PE) is activated on JMP signal to 
  //   jump to second part of uCode (go to T=16)
  //   IC inc (CP) is activated by falling CLK
  //   Generate control bus
  //   Both IRs are set 
  //   to 0x00 when 
  //   INT must be
  //   handled
  //   Next IR is loaded on 
  //   rising CLK
  //   Value loaded in Next IR is 
  //   presented to control bus 
  //   by IR on falling CLK
  //   contents of Control Word #3 (hex, n*v repeats v):
  //   /Users/Vittorio.Nardone/Documents/__private__/sap-project/roms/cw3-rom.hex false
  //   contents of Registers Control Word (hex, n*v repeats v):
  //   /Users/Vittorio.Nardone/Documents/__private__/sap-project/roms/cw7-rom.hex false
  //   contents of Control Word #2 (hex, n*v repeats v):
  //   /Users/Vittorio.Nardone/Documents/__private__/sap-project/roms/cw2-rom.hex false
  //   contents of ROM (hex, n*v repeats v):
  //   /Users/Vittorio.Nardone/Documents/__private__/sap-project/roms/kernel-rom.hex false
  //   contents of Control Word #1 (hex, n*v repeats v):
  //   /Users/Vittorio.Nardone/Documents/__private__/sap-project/roms/cw1-rom.hex false
  //   contents of PC/SP Control Word (hex, n*v repeats v):
  //   /Users/Vittorio.Nardone/Documents/__private__/sap-project/roms/cw9-rom.hex false
  //   contents of Control Word #6 (hex, n*v repeats v):
  //   /Users/Vittorio.Nardone/Documents/__private__/sap-project/roms/cw6-rom.hex false
  //   contents of Control Word #5 (hex, n*v repeats v):
  //   /Users/Vittorio.Nardone/Documents/__private__/sap-project/roms/cw5-rom.hex false
  //   contents of Control Word #4 (hex, n*v repeats v):
  //   /Users/Vittorio.Nardone/Documents/__private__/sap-project/roms/cw4-rom.hex false
  //   contents of Instructions Control Word (hex, n*v repeats v):
  //   /Users/Vittorio.Nardone/Documents/__private__/sap-project/roms/cw8-rom.hex false
endmodule
